// Logisim project simulation.circ as structural Verilog: 1 circuit, main circuit main
module main (
  input  A0,
  input  B0,
  input  A1,
  input  B1,
  input  in_5,
  input  in_6,
  input  I1,
  input  I0,
  output out_9,
  output out_10,
  output out_11
);

  wire multiplexer_1_out, multiplexer_2_out, multiplexer_3_out, multiplexer_6_out, U3A_out, U3B_out, U3C_out,
       U3D_out, U4A_out, U4B_out, U4C_out, U4D_out, U5B_out, U5C_out, U5D_out, U6A_out, U6B_out, U6C_out,
       U6D_out, U7A_out, U7B_out, U7D_out;

  and U7A (U7A_out, A0, B0);
  or U4A (U4A_out, A0, B0);
  nand U5C (U5C_out, B0, B0);
  nand U5D (U5D_out, B1, B1);
  Multiplexer multiplexer_1 (.in0(U7A_out), .in1(U4A_out), .out(multiplexer_1_out), .sel(I0));
  Multiplexer multiplexer_2 (.in0(B0), .in1(U5C_out), .out(multiplexer_2_out), .sel(I0));
  Multiplexer multiplexer_3 (.in0(B1), .in1(U5D_out), .out(multiplexer_3_out), .sel(I0));
  xor U3A (U3A_out, A0, multiplexer_2_out);
  and U6C (U6C_out, multiplexer_2_out, A0);
  xor U3B (U3B_out, A1, multiplexer_3_out);
  and U6D (U6D_out, multiplexer_3_out, A1);
  xor U3C (U3C_out, U3A_out, I0);
  and U6A (U6A_out, I0, U3A_out);
  and U6B (U6B_out, U6C_out, U3B_out);
  or U4C (U4C_out, U6A_out, U6C_out);
  or U4B (U4B_out, U6B_out, U6D_out);
  xor U3D (U3D_out, U4C_out, U3B_out);
  and U7B (U7B_out, U3A_out, I0);
  and U7D (U7D_out, U3B_out, U7B_out);
  or U4D (U4D_out, U7D_out, U4B_out);
  Multiplexer multiplexer_4 (.in0(multiplexer_1_out), .in1(U3C_out), .out(out_9), .sel(I1));
  Multiplexer multiplexer_5 (.in0(in_5), .in1(U3D_out), .out(out_10), .sel(I1));
  Multiplexer multiplexer_6 (.in0(in_6), .in1(U4D_out), .out(multiplexer_6_out), .sel(I1));
  nand U5B (U5B_out, I0, I0);
  and U7C (out_11, multiplexer_6_out, U5B_out);

  // Notes on the sheet:
  //   00 -- AND
  //   01 -- OR
  //   10 -- ADD
  //   11 -- SUBT
  //   Cin --
  //   A0
  //   B0
  //   A0
  //   B0
  //   => 0 for ADD, 1 for SUBT
  //   A0
  //   B0
  //   ~B0
  //   taken from last bit
  //   A1
  //   B1
  //   ~B1
  //   X0/X1?
  //   G0
  //   G1
  //   P0
  //   P1
  //   SUM0 / DIFF0
  //   SUM1/DIFF1
  //   oveflow (SUM2)
  //   0X/1X?
  //   AND 0 on I1
  //   only displays overflow
  //   if instruction is 1 on I0 
endmodule
